# Fritzing sketch Untitled Sketch (saved by Fritzing 0.9.4)
breadboards: 1

parts:
  Компонент1 = Arduino Mega 2560 (Rev3)
  BT1 = Bluetooth HC-06u [package=THT]
  M4 = DC Motor  # not connected
  M5 = DC Motor
  DC_Mot_Enc1 = DC Motor with two-phase hall-encoder [part_number=VT-E-G25A-06-177E]
  M6 = DC Motor
  M7 = DC Motor  # not connected
  DC_Mot_Enc3 = DC Motor with two-phase hall-encoder [part_number=VT-E-G25A-06-177E]
  Power_plug1 = Power plug  # not connected

nets:
  N1: Компонент1.D15/RX3, BT1.TXD
  N2: Компонент1.D14/TX3, BT1.RXD
  GND: Компонент1.GND, BT1.GND, DC_Mot_Enc1.pin5
  5V: Компонент1.5V, BT1.VCC, DC_Mot_Enc1.pin2
  N3: Компонент1.D3_PWM, DC_Mot_Enc1.pin3
  N4: M5.pin_1, DC_Mot_Enc1.pin1
  N5: M5.pin_2, DC_Mot_Enc1.pin6
  N6: M6.pin_1, DC_Mot_Enc3.pin1, DC_Mot_Enc3.pin2
  N7: M6.pin_2, DC_Mot_Enc3.pin6

custom parts:
  Bluetooth HC-06u: Bluetooth HC-06 - face up, pins down 16.5mm x 37.5mm PCB
